// Logisim project bloqueB.circ as structural Verilog: 1 circuit, main circuit BloqueB
module BloqueB (
  input  Cin,
  input  Pl,
  input  Gl,
  input  Ph,
  input  Gh,
  output Cl,
  output Ch,
  output Phl,
  output Ghl
);

  wire and_1_out, and_3_out;

  and and_1 (and_1_out, Cin, Pl);
  and and_2 (Phl, Ph, Pl);
  and and_3 (and_3_out, Ph, Gl);
  or or_1 (Ch, and_1_out, Gl);
  or or_2 (Ghl, and_3_out, Gh);

  assign Cl = Cin;
endmodule
