// Logisim project compuertaFA.circ as structural Verilog: 1 circuit, main circuit FAGP
module FAGP (
  input  A,
  input  B,
  input  ci,
  output si,
  output pi,
  output gi
);

  wire compxor_1_f;

  or or_1 (pi, A, B);
  and and_1 (gi, A, B);
  compXOR compxor_1 (.A(A), .B(B), .F(compxor_1_f));
  compXOR compxor_2 (.A(compxor_1_f), .B(ci), .F(si));
endmodule
