// Logisim project compuertaXOR.circ as structural Verilog: 1 circuit, main circuit compXOR
module compXOR (
  input  A,
  input  B,
  output F
);

  wire and_1_out, and_2_out, not_1_out, not_2_out;

  not not_1 (not_1_out, B);
  not not_2 (not_2_out, A);
  and and_1 (and_1_out, A, not_1_out);
  and and_2 (and_2_out, not_2_out, B);
  or or_1 (F, and_1_out, and_2_out);
endmodule
