// Logisim project proyectoArqui.circ as structural Verilog: 1 circuit, main circuit SUMLAT
module SUMLAT (
  input  in_1,
  input  [7:0] A,
  input  [7:0] B,
  output out_4,
  output out_5,
  output out_6,
  output out_7,
  output out_8,
  output out_9,
  output out_10,
  output out_11,
  output out_12,
  output out_13
);

  wire bloqueb_1_ch, bloqueb_1_cl, bloqueb_1_ghl, bloqueb_1_phl, bloqueb_2_ch, bloqueb_2_cl, bloqueb_2_ghl,
       bloqueb_2_phl, bloqueb_3_ch, bloqueb_3_cl, bloqueb_3_ghl, bloqueb_3_phl, bloqueb_4_ch, bloqueb_4_cl,
       bloqueb_4_ghl, bloqueb_4_phl, bloqueb_5_ch, bloqueb_5_cl, bloqueb_5_ghl, bloqueb_5_phl, bloqueb_6_ch,
       bloqueb_6_cl, bloqueb_6_ghl, bloqueb_6_phl, bloqueb_7_ch, bloqueb_7_cl, fagp_1_gi, fagp_1_pi,
       fagp_2_gi, fagp_2_pi, fagp_3_gi, fagp_3_pi, fagp_4_gi, fagp_4_pi, fagp_5_gi, fagp_5_pi, fagp_6_gi,
       fagp_6_pi, fagp_7_gi, fagp_7_pi, fagp_8_gi, fagp_8_pi;

  FAGP fagp_1 (.A(A[0]), .B(B[0]), .ci(bloqueb_1_cl), .si(out_4), .pi(fagp_1_pi), .gi(fagp_1_gi));
  FAGP fagp_2 (.A(A[1]), .B(B[1]), .ci(bloqueb_1_ch), .si(out_5), .pi(fagp_2_pi), .gi(fagp_2_gi));
  FAGP fagp_3 (.A(A[2]), .B(B[2]), .ci(bloqueb_2_cl), .si(out_6), .pi(fagp_3_pi), .gi(fagp_3_gi));
  FAGP fagp_4 (.A(A[3]), .B(B[3]), .ci(bloqueb_2_ch), .si(out_7), .pi(fagp_4_pi), .gi(fagp_4_gi));
  FAGP fagp_5 (.A(A[4]), .B(B[4]), .ci(bloqueb_3_cl), .si(out_10), .pi(fagp_5_pi), .gi(fagp_5_gi));
  FAGP fagp_6 (.A(A[5]), .B(B[5]), .ci(bloqueb_3_ch), .si(out_11), .pi(fagp_6_pi), .gi(fagp_6_gi));
  FAGP fagp_7 (.A(A[6]), .B(B[6]), .ci(bloqueb_4_cl), .si(out_12), .pi(fagp_7_pi), .gi(fagp_7_gi));
  FAGP fagp_8 (.A(A[7]), .B(B[7]), .ci(bloqueb_4_ch), .si(out_13), .pi(fagp_8_pi), .gi(fagp_8_gi));
  BloqueB bloqueb_1 (
    .Cin(bloqueb_5_cl), .Pl(fagp_1_pi), .Gl(fagp_1_gi), .Ph(fagp_2_pi), .Gh(fagp_2_gi), .Cl(bloqueb_1_cl),
    .Ch(bloqueb_1_ch), .Phl(bloqueb_1_phl), .Ghl(bloqueb_1_ghl));
  BloqueB bloqueb_2 (
    .Cin(bloqueb_5_ch), .Pl(fagp_3_pi), .Gl(fagp_3_gi), .Ph(fagp_4_pi), .Gh(fagp_4_gi), .Cl(bloqueb_2_cl),
    .Ch(bloqueb_2_ch), .Phl(bloqueb_2_phl), .Ghl(bloqueb_2_ghl));
  BloqueB bloqueb_3 (
    .Cin(bloqueb_6_cl), .Pl(fagp_5_pi), .Gl(fagp_5_gi), .Ph(fagp_6_pi), .Gh(fagp_6_gi), .Cl(bloqueb_3_cl),
    .Ch(bloqueb_3_ch), .Phl(bloqueb_3_phl), .Ghl(bloqueb_3_ghl));
  BloqueB bloqueb_4 (
    .Cin(bloqueb_6_ch), .Pl(fagp_7_pi), .Gl(fagp_7_gi), .Ph(fagp_8_pi), .Gh(fagp_8_gi), .Cl(bloqueb_4_cl),
    .Ch(bloqueb_4_ch), .Phl(bloqueb_4_phl), .Ghl(bloqueb_4_ghl));
  BloqueB bloqueb_5 (
    .Cin(bloqueb_7_cl), .Pl(bloqueb_1_phl), .Gl(bloqueb_1_ghl), .Ph(bloqueb_2_phl), .Gh(bloqueb_2_ghl),
    .Cl(bloqueb_5_cl), .Ch(bloqueb_5_ch), .Phl(bloqueb_5_phl), .Ghl(bloqueb_5_ghl));
  BloqueB bloqueb_6 (
    .Cin(bloqueb_7_ch), .Pl(bloqueb_3_phl), .Gl(bloqueb_3_ghl), .Ph(bloqueb_4_phl), .Gh(bloqueb_4_ghl),
    .Cl(bloqueb_6_cl), .Ch(bloqueb_6_ch), .Phl(bloqueb_6_phl), .Ghl(bloqueb_6_ghl));
  BloqueB bloqueb_7 (
    .Cin(in_1), .Pl(bloqueb_5_phl), .Gl(bloqueb_5_ghl), .Ph(bloqueb_6_phl), .Gh(bloqueb_6_ghl),
    .Cl(bloqueb_7_cl), .Ch(bloqueb_7_ch), .Phl(out_8), .Ghl(out_9));
endmodule
